# Fritzing sketch Diffuser Device (saved by Fritzing 0.9.9b)
breadboards: 1

parts:
  Mod1 = KY-005 Infrared Transmitter Module [package="Breakout board"]
  Part1 = Adafruit Feather M0 WINC1500 [part_number="Adafruit #3010"]
  Part2 = Lithium Ion Polymer Battery 3.7v 2000mAh [part_number=2011]  # not connected

nets:
  N1: Mod1.S, Part1.GND
  VIN: Mod1.Vin, Part1.+3V3
  N2: Mod1.-, Part1.D9

custom parts:
  KY-005 Infrared Transmitter Module: Arduino IR Transmitter Module Keyes KY-005, emits infrared light at 38KHz.
  Adafruit Feather M0 WINC1500: This is the Adafruit Feather M0 WiFi w/ATWINC1500 - our take on an 'all-in-one' Arduino-compatible + high speed, reliable WiFi with built in USB and battery charging. Its an Adafruit Feather M0 with a WiFi module, ready to rock! Connect your Feather to the Internet with this fine new FCC-certified WiFi module from Atmel. This 802.11bgn-capable WiFi module is the best new thing for networking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
  Lithium Ion Polymer Battery 3.7v 2000mAh: Lithium ion polymer (also known as 'lipo' or 'lipoly') batteries are thin, light and powerful. The output ranges from 4.2V when completely charged to 3.7V. This battery has a capacity of 2000mAh. The batteries come pre-attached with a genuine 2-pin JST-PH connector as shown and include the necessary protection circuitry.
